# Fritzing sketch OpenSpool (saved by Fritzing 1.0.4)

parts:
  Part1 = PN532 Elechouse RFID NFC Module V3
  A1 = Wemos-s2-mini_1 [part_number="WeMos D1 Mini Lite"]

nets:
  N1: Part1.SCK, A1.connector29
  N2: Part1.MISO, A1.connector22
  N3: Part1.MOSI, A1.connector21
  N4: Part1.SS, A1.connector28
  N5: Part1.VCC, A1.connector16
  N6: Part1.GND, A1.connector17

custom parts:
  PN532 Elechouse RFID NFC Module V3: NFC is a popular technology in recent years. We often heard this work while smart phone company such as Samsung or HTC introduces their latest high-end phones. Almost all the high-end phone in the market support NFC. Near field communication (NFC) is a set of standards for smart phones and similar devices to establish radio communication with each other by touching them together or bringing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
